# Fritzing sketch Untitled Sketch 2 (saved by Fritzing 0.9.3b)
breadboards: 2

parts:
  Composant2 = Soil Moisture Sensor
  L1 = Inductor [package="0805 [SMD]"]
  C1 = Electrolytic Capacitor [capacitance=10μF package="0605 [SMD, electrolytic]"]
  U1 = POT [package=pot_mammoth]
  U2 = 4-Channel 5v Relay Shield [package=relay-4ch5v10a]
  WATER_PUMP1 = water pump/motor  # not connected
  WATER_PUMP2 = water pump/motor  # not connected
  WATER_PUMP3 = water pump/motor  # not connected
  WATER_PUMP4 = water pump/motor  # not connected
  BAT1 = 12 battery [package=battery]
  R1 = Resistor [tolerance=±5% resistance=220 package="2010 [SMD]"]
  R2 = Resistor [tolerance=±5% resistance=220 package="2010 [SMD]"]
  R3 = Resistor [tolerance=±5% resistance=220 package="2010 [SMD]"]
  R4 = Resistor [tolerance=±5% resistance=220 package="2010 [SMD]"]
  U3 = TRANSISTOR_NPN_2 [package=to-92]
  U4 = TRANSISTOR_NPN_2 [package=to-92]
  U5 = TRANSISTOR_NPN_2 [package=to-92]
  U6 = TRANSISTOR_NPN_2 [package=to-92]
  DHT1 = DHT11 Humitidy and Temperature Sensor
  DHT2 = DHT11 Humitidy and Temperature Sensor
  U7 = POT [package=pot_alpha_rv16af-20]
  U8 = POT [package=pot_alpha_rv16af-20]
  LCD1 = LCD screen  # not connected
  U9 = POT [package=pot_mammoth]  # not connected
  Composant1 = Arduino Mega 2560 (Rev3)
  Composant3 = Soil Moisture Sensor
  L2 = Inductor [package="0805 [SMD]"]
  C2 = Electrolytic Capacitor [capacitance=10μF package="0605 [SMD, electrolytic]"]
  U10 = POT [package=pot_alpha_rv16af-20]
  Composant4 = ESP-WROOM-32 [ESP-32S] Module [part_number=ESP-WROOM-32]
  R5 = Photocell (LDR) [package=THT]
  R6 = Resistor [tolerance=±5% resistance=220 package="2010 [SMD]"]
  Composant5 = Soil Moisture Sensor
  L3 = Inductor [package="0805 [SMD]"]
  C3 = Electrolytic Capacitor [capacitance=10μF package="0605 [SMD, electrolytic]"]
  U11 = POT [package=pot_alpha_rv16af-20]
  U12 = POT [package=pot_mammoth]
  L4 = Inductor [package="0805 [SMD]"]
  C4 = Electrolytic Capacitor [capacitance=10μF package="0605 [SMD, electrolytic]"]
  Composant6 = Soil Moisture Sensor

nets:
  N1: Composant2.SIG, U1.A, Composant1.A3
  GND: Composant2.GND, C1.-, U1.E, U2.GND, U2.K1-Off, U2.K1-On, U2.K2-Off, U2.K2-On, U2.K3-Off, U2.K3-On, U2.K4-Off, U2.K4-On, BAT1.-, BAT1.+, U3.E, U4.E, U5.E, U6.E, DHT1.GND, DHT2.GND, U7.E, U8.E, Composant1.GND, Composant3.GND, L2.pin_0, C2.-, U10.A, U10.E, Composant4.GND, R6.Pin_0, Composant5.GND, L3.pin_0, C3.-, U11.A, U11.E, U12.S, U12.E, L4.pin_0, C4.-
  N2: Composant2.VCC, L1.pin_1, C1.+
  VDD: L1.pin_0, U1.S, U2.VCC, DHT1.VDD, DHT2.VDD, U7.A, U8.A, Composant1.5V, R5.pin_0
  N3: U2.IN1, U6.C
  N4: U2.IN2, U5.C
  N5: U2.IN4, U3.C
  N6: U2.IN3, U4.C
  N7: R1.Pin_0, Composant1.D7_PWM
  N8: R1.Pin_1, U3.B
  N9: R2.Pin_0, Composant1.D6_PWM
  N10: R2.Pin_1, U4.B
  N11: R3.Pin_0, Composant1.D5_PWM
  N12: R3.Pin_1, U5.B
  N13: R4.Pin_0, Composant1.D4_PWM
  N14: R4.Pin_1, U6.B
  N15: DHT1.DATA, Composant1.D3_PWM
  N16: DHT2.DATA, Composant1.D2_PWM
  N17: U7.S, Composant1.A0
  N18: U8.S, Composant1.A1
  N19: Composant1.A2, R5.pin_1, R6.Pin_1
  N20: Composant1.A5, Composant5.SIG, U11.S
  N21: Composant1.A6, U12.A, Composant6.SIG
  N22: Composant1.D0_RX0, Composant4.SD3
  N23: Composant1.D1_TX0, Composant4.SD2
  N24: Composant3.SIG, U10.S
  N25: Composant3.VCC, L2.pin_1
  N26: Composant5.VCC, L3.pin_1
  N27: L4.pin_1, Composant6.VCC

custom parts:
  4-Channel 5v Relay Shield: 4 Channel 5v Relay Shield w. 2x SPD-06VDC-SD-C
  water pump/motor: WATER PUMP BY ARDUBLOCKTR
  12 battery: 12V lead acid type battery, like the Husqvarna YTH2448 12V 35AH battery. The pads in pcb are sized to accomidate up to 14ga wire (as these batterys will deliver high currents.)
  DHT11 Humitidy and Temperature Sensor: DHT11 Humidity and Temperature Sensor
  ESP-WROOM-32 [ESP-32S] Module: Espressif ESP-WROOM-32 WiFi/Bluetooth LE microcontroller module also known as the Ai-Thinker ESP-32S module with similar formfactor. The ESP32 is a microcontroller chip with WiFi and BLE capabilities. The chip is developed by Espressif and is the successor to the popular ESP8266 WiFi module.
