# Fritzing sketch diallvo_fritzing (saved by Fritzing 0.8.7b)
breadboards: 1

parts:
  Composant1 = Arduino Mega 2560 (Rev3)
  Composant2 = Adafruit ESP32-S3 Feather [part_number="Adafruit #5323"]
  Adafruit_Simple_Soil_Moisture_Sensor1 = Adafruit Simple Soil Moisture Sensor [part_number=#6362]
  Adafruit_Simple_Soil_Moisture_Sensor2 = Adafruit Simple Soil Moisture Sensor [part_number=#6362]
  Adafruit_Simple_Soil_Moisture_Sensor3 = Adafruit Simple Soil Moisture Sensor [part_number=#6362]
  Adafruit_Simple_Soil_Moisture_Sensor4 = Adafruit Simple Soil Moisture Sensor [part_number=#6362]
  U1 = Module 4 Relais 5V [package="Module 4 Relais 5V"]
  WATER_PUMP1 = water pump/motor
  WATER_PUMP2 = water pump/motor
  WATER_PUMP3 = water pump/motor
  WATER_PUMP4 = water pump/motor
  DHT1 = DHT11 Humitidy and Temperature Sensor
  DHT2 = DHT11 Humitidy and Temperature Sensor
  J4 = Piezo Speaker
  R1 = Photocell (LDR) [package=THT]
  BAT1 = 12 battery [package=battery]
  R2 = 330 Ω Resistor [package="0603 [SMD]"]  # not connected
  R3 = 330 Ω Resistor [package="0603 [SMD]"]

nets:
  N1: Composant1.A0, R1.pin_1
  N2: Composant1.A1, Adafruit_Simple_Soil_Moisture_Sensor2.SIGNAL
  N3: Composant1.A2, Adafruit_Simple_Soil_Moisture_Sensor3.SIGNAL
  N4: Composant1.A3, Adafruit_Simple_Soil_Moisture_Sensor1.SIGNAL
  N5: Composant1.A4, Adafruit_Simple_Soil_Moisture_Sensor4.SIGNAL
  GND: Composant1.GND, Composant2.GND
  N6: Composant1.D0_RX0, Composant2.RX
  N7: Composant1.D1_TX0, Composant2.TX
  N8: Composant1.D2_PWM, DHT1.DATA
  N9: Composant1.D3_PWM, DHT2.DATA
  N10: Composant1.D4_PWM, U1.IN1
  N11: Composant1.D5_PWM, U1.IN2
  N12: Composant1.D6_PWM, U1.IN3
  N13: Composant1.D7_PWM, U1.IN4
  VDD: Adafruit_Simple_Soil_Moisture_Sensor1.V+, Adafruit_Simple_Soil_Moisture_Sensor2.V+, Adafruit_Simple_Soil_Moisture_Sensor3.V+, Adafruit_Simple_Soil_Moisture_Sensor4.V+, DHT1.VDD, DHT2.VDD, J4.pin2, R1.pin_0
  GND_2: Adafruit_Simple_Soil_Moisture_Sensor1.GND, Adafruit_Simple_Soil_Moisture_Sensor2.GND, Adafruit_Simple_Soil_Moisture_Sensor3.GND, Adafruit_Simple_Soil_Moisture_Sensor4.GND, DHT1.GND, DHT2.GND, J4.pin1, R3.Pin_0
  N14: U1.VCC, BAT1.+
  N15: U1.GND, BAT1.-
  N16: U1.K1-NF, WATER_PUMP4.pin_2
  N17: U1.K2-NF, WATER_PUMP3.pin_2
  N18: U1.K3-NF, WATER_PUMP2.pin_2
  N19: U1.K4-NF, WATER_PUMP1.pin_2
  N20: U1.K1-NO, WATER_PUMP4.pin_1
  N21: U1.K2-NO, WATER_PUMP3.pin_1
  N22: U1.K3-NO, WATER_PUMP2.pin_1
  N23: U1.K4-NO, WATER_PUMP1.pin_1

custom parts:
  Adafruit ESP32-S3 Feather: The ESP32-S3 has arrived in Feather format - and what a great way to get started with this powerful new chip from Espressif! With dual 240 MHz cores, WiFi and BLE support, and native USB, this Feather is great for powering your IoT projects. That's right - it's the new Adafruit ESP32-S3 Feather! With native USB and 8 MB flash, this board will let you upgrade your existing ESP32 projects.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
  Adafruit Simple Soil Moisture Sensor: Perfect for educational uses, the Adafruit Simple Soil Moisture Sensor is low cost, and easy to use. This is a simple resistive style moisture sensor, where there's two prongs and the sensor measures the conductivity between the two. We gold-plated the prongs so reduce risk of oxidation - if you see build-up on the prongs, clean them off with a dish-scrubber to keep the sensor going. While not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
  Module 4 Relais 5V: Module 4 Relais 5V 4x SPD-06VDC-SD-C
  water pump/motor: WATER PUMP BY ARDUBLOCKTR
  DHT11 Humitidy and Temperature Sensor: DHT11 Humidity and Temperature Sensor
  Photocell (LDR): A generic light dependent resistor (LDR)
  12 battery: 12V lead acid type battery, like the Husqvarna YTH2448 12V 35AH battery. This is the mini version 1/4 the size of the actual battery to be closer to typical breadboard parts (around 2in wide rathher than 7in). The pads in pcb are sized to accomidate up to 14ga wire (as these batterys will deliver high currents.)
  330 Ω Resistor: A generic resistor (0.25W)
